# Fritzing sketch ShiftRegister (saved by Fritzing 0.9.3b)
breadboards: 3

parts:
  IC1 = SHIFT REGISTER [package=dil16]
  Q1 = NPN-Transistor [package="TO92 [THT]"]
  Q2 = NPN-Transistor [package="TO92 [THT]"]
  Q3 = NPN-Transistor [package="TO92 [THT]"]
  Q4 = NPN-Transistor [package="TO92 [THT]"]
  Q5 = NPN-Transistor [package="TO92 [THT]"]
  Q6 = NPN-Transistor [package="TO92 [THT]"]
  Q7 = NPN-Transistor [package="TO92 [THT]"]
  Q8 = NPN-Transistor [package="TO92 [THT]"]
  R1 = Resistor [tolerance=±5% resistance=220 package="2010 [SMD]"]
  R2 = Resistor [tolerance=±5% resistance=220 package="2010 [SMD]"]
  R3 = Resistor [tolerance=±5% resistance=220 package="2010 [SMD]"]
  R4 = Resistor [tolerance=±5% resistance=220 package="2010 [SMD]"]
  R5 = Resistor [tolerance=±5% resistance=220 package="2010 [SMD]"]
  R6 = Resistor [tolerance=±5% resistance=220 package="2010 [SMD]"]
  R7 = Resistor [tolerance=±5% resistance=220 package="2010 [SMD]"]
  R8 = Resistor [tolerance=±5% resistance=220 package="2010 [SMD]"]
  Q9 = NPN-Transistor [package="TO92 [THT]"]
  IC2 = SHIFT REGISTER [package=dil16]
  Q10 = NPN-Transistor [package="TO92 [THT]"]
  Q11 = NPN-Transistor [package="TO92 [THT]"]
  Q12 = NPN-Transistor [package="TO92 [THT]"]
  Q13 = NPN-Transistor [package="TO92 [THT]"]
  Q14 = NPN-Transistor [package="TO92 [THT]"]
  Q15 = NPN-Transistor [package="TO92 [THT]"]
  R9 = Resistor [tolerance=±5% resistance=220 package="2010 [SMD]"]
  R10 = Resistor [tolerance=±5% resistance=220 package="2010 [SMD]"]
  R11 = Resistor [tolerance=±5% resistance=220 package="2010 [SMD]"]
  R12 = Resistor [tolerance=±5% resistance=220 package="2010 [SMD]"]
  R13 = Resistor [tolerance=±5% resistance=220 package="2010 [SMD]"]
  R14 = Resistor [tolerance=±5% resistance=220 package="2010 [SMD]"]
  R15 = Resistor [tolerance=±5% resistance=220 package="2010 [SMD]"]
  R16 = Resistor [tolerance=±5% resistance=220 package="2010 [SMD]"]
  Q16 = NPN-Transistor [package="TO92 [THT]"]
  Q17 = NPN-Transistor [package="TO92 [THT]"]
  IC3 = SHIFT REGISTER [package=dil16]
  Q18 = NPN-Transistor [package="TO92 [THT]"]
  Q19 = NPN-Transistor [package="TO92 [THT]"]
  Q20 = NPN-Transistor [package="TO92 [THT]"]
  Q21 = NPN-Transistor [package="TO92 [THT]"]
  Q22 = NPN-Transistor [package="TO92 [THT]"]
  Q23 = NPN-Transistor [package="TO92 [THT]"]
  R17 = Resistor [tolerance=±5% resistance=220 package="2010 [SMD]"]
  R18 = Resistor [tolerance=±5% resistance=220 package="2010 [SMD]"]
  R19 = Resistor [tolerance=±5% resistance=220 package="2010 [SMD]"]
  R20 = Resistor [tolerance=±5% resistance=220 package="2010 [SMD]"]
  R21 = Resistor [tolerance=±5% resistance=220 package="2010 [SMD]"]
  R22 = Resistor [tolerance=±5% resistance=220 package="2010 [SMD]"]
  R23 = Resistor [tolerance=±5% resistance=220 package="2010 [SMD]"]
  R24 = Resistor [tolerance=±5% resistance=220 package="2010 [SMD]"]
  Q24 = NPN-Transistor [package="TO92 [THT]"]
  Part1 = Arduino Leonardo (Rev3b)

nets:
  N1: IC1.QB, Q2.B
  N2: IC1.QC, Q3.B
  N3: IC1.QD, Q6.B
  N4: IC1.QE, Q4.B
  N5: IC1.QF, Q5.B
  N6: IC1.QG, Q7.B
  N7: IC1.QH, Q8.B
  N8: IC1.GND, IC1.G
  N9: IC1.QH*, IC2.SER
  N10: IC1.SCL, IC1.VCC, Q1.C, Q2.C, Q3.C, Q4.C, Q5.C, Q6.C, Q7.C, Q8.C
  N11: IC1.SCK, IC2.SCK, IC3.SCK, Part1.D10_PWM/A10
  N12: IC1.RCK, IC2.RCK, IC3.RCK, Part1.D9_PWM/A9
  N13: IC1.SER, Part1.D8/A8
  N14: IC1.QA, Q1.B
  N15: Q1.E, R2.Pin_0
  N16: Q2.E, R4.Pin_0
  N17: Q3.E, R6.Pin_0
  N18: Q4.E, R1.Pin_0
  N19: Q5.E, R3.Pin_0
  N20: Q6.E, R8.Pin_0
  N21: Q7.E, R5.Pin_0
  N22: Q8.E, R7.Pin_0
  N23: Q9.E, R15.Pin_0
  N24: Q9.B, IC2.QH
  N25: Q9.C, IC2.SCL, IC2.VCC, Q10.C, Q11.C, Q12.C, Q13.C, Q14.C, Q15.C, Q16.C
  N26: IC2.QB, Q11.B
  N27: IC2.QC, Q12.B
  N28: IC2.QD, Q14.B
  N29: IC2.QE, Q16.B
  N30: IC2.QF, Q13.B
  N31: IC2.QG, Q15.B
  N32: IC2.GND, IC2.G
  N33: IC2.QH*, IC3.SER
  N34: IC2.QA, Q10.B
  N35: Q10.E, R12.Pin_0
  N36: Q11.E, R10.Pin_0
  N37: Q12.E, R14.Pin_0
  N38: Q13.E, R11.Pin_0
  N39: Q14.E, R16.Pin_0
  N40: Q15.E, R9.Pin_0
  N41: R13.Pin_0, Q16.E
  N42: Q17.E, R23.Pin_0
  N43: Q17.B, IC3.QH
  N44: Q17.C, IC3.SCL, IC3.VCC, Q18.C, Q19.C, Q20.C, Q21.C, Q22.C, Q23.C, Q24.C
  N45: IC3.QB, Q19.B
  N46: IC3.QC, Q20.B
  N47: IC3.QD, Q22.B
  N48: IC3.QE, Q24.B
  N49: IC3.QF, Q21.B
  N50: IC3.QG, Q23.B
  N51: IC3.GND, IC3.G
  N52: IC3.QA, Q18.B
  N53: Q18.E, R20.Pin_0
  N54: Q19.E, R18.Pin_0
  N55: Q20.E, R22.Pin_0
  N56: Q21.E, R19.Pin_0
  N57: Q22.E, R24.Pin_0
  N58: Q23.E, R17.Pin_0
  N59: R21.Pin_0, Q24.E

notes:
  1
  2
  3
  4
  5
  6
  7
  8
